# Fritzing sketch wiring (saved by Fritzing 0.9.10b)
breadboards: 1

parts:
  Part1 = HT16K33 Breakout 16x8 LED Matrix Driver [part_number=1427]
  Part2 = Adafruit MAX9814 Electret Microphone Amplifier [part_number="Adafruit #1713"]
  BeagleBone1 = BeagleBone Black
  R1 = Resistor [tolerance=±5% power=0.25 resistance=1.5k package=THT]
  R2 = Resistor [tolerance=±5% power=0.25 resistance=1.8k package=THT]
  R3 = Resistor [tolerance=±5% power=0.25 resistance=47k package=THT]
  R4 = Resistor [tolerance=±5% power=0.25 resistance=4.7k package=THT]

nets:
  N1: Part1.SCL, BeagleBone1.no_name_yet#19, R3.Pin_1
  N2: Part1.SDA, BeagleBone1.no_name_yet#20, R4.Pin_1
  VDD: Part1.VDD, Part2.VDD, Part2.GAIN, BeagleBone1.no_name_yet#3, R3.Pin_0, R4.Pin_0
  GND: Part1.GND, Part2.GND, BeagleBone1.no_name_yet#1, BeagleBone1.no_name_yet#34, R2.Pin_0
  N3: Part2.OUTPUT, R1.Pin_0
  N4: BeagleBone1.no_name_yet#39, BeagleBone1.no_name_yet#40, R1.Pin_1, R2.Pin_1

custom parts:
  HT16K33 Breakout 16x8 LED Matrix Driver: This is the magic sauce in our 7-segment and matrix backpacks, now available in breadboard-friendly breakout board format. The HT16K33 is a neat little chip that has the ability to drive a multiplexed 16x8 matrix (that's 128 individual LEDs). The communication protocol is I2C so it uses only 2 pins, and you can have up to 8 selectable I2C addresses so thats a total of 8 matrices, each one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
  Adafruit MAX9814 Electret Microphone Amplifier: Add an ear to your project with this well-designed electret microphone amplifier with AGC. This fully assembled and tested board comes with a 20-20KHz electret microphone soldered on. For the amplification, we use the Maxim MAX9814, a specialty chip that is designed for amplifying electret microphones in situations where the loudness of the audio isn't predictable. This fancy microphone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
  BeagleBone Black: BeagleBone Black rev. A5B
